# Fritzing sketch UserBot-8Outputs-DHT (saved by Fritzing 0.9.3b)
circuit board: 6.88566cm x 5.36311cm
breadboards: 1

parts:
  LED3 = LED - 5mm [color="Red (633nm)" package="5 mm [THT]"]
  LED5 = LED - 5mm [color="Red (633nm)" package="5 mm [THT]"]
  R1 = Resistor [tolerance=±5% resistance=220 package=THT]
  R2 = Resistor [tolerance=±5% resistance=220 package=THT]
  R3 = Resistor [tolerance=±5% resistance=220 package=THT]
  R4 = Resistor [tolerance=±5% resistance=220 package=THT]
  Arduino1 = Arduino Uno (Rev3)
  LED6 = LED - 5mm [color="Red (633nm)" package="5 mm [THT]"]
  LED7 = LED - 5mm [color="Red (633nm)" package="5 mm [THT]"]
  LED8 = LED - 5mm [color="Red (633nm)" package="5 mm [THT]"]
  LED9 = LED - 5mm [color="Red (633nm)" package="5 mm [THT]"]
  LED10 = LED - 5mm [color="Red (633nm)" package="5 mm [THT]"]
  LED11 = LED - 5mm [color="Red (633nm)" package="5 mm [THT]"]
  R6 = Resistor [tolerance=±5% resistance=220 package=THT]
  R7 = Resistor [tolerance=±5% resistance=220 package=THT]
  R8 = Resistor [tolerance=±5% resistance=220 package=THT]
  R9 = Resistor [tolerance=±5% resistance=220 package=THT]
  RHT2 = Humidity and Temperature Sensor RHT03 [part_number=DHT22]

nets:
  N1: LED3.cathode, R1.Pin_0
  N2: LED3.anode, Arduino1.D3_PWM
  N3: LED5.cathode, R2.Pin_0
  N4: LED5.anode, Arduino1.D4
  N5: R1.Pin_1, R2.Pin_1, R3.Pin_1, R4.Pin_1, Arduino1.GND, R6.Pin_1, R7.Pin_1, R8.Pin_1, R9.Pin_1, RHT2.GND_2
  N6: R3.Pin_0, LED6.cathode
  N7: R4.Pin_0, LED11.cathode
  N8: Arduino1.A0, LED10.anode
  N9: Arduino1.A1, LED11.anode
  N10: Arduino1.A2, RHT2.Data-signal
  N11: Arduino1.D8, LED9.anode
  N12: Arduino1.D5_PWM, LED6.anode
  N13: Arduino1.D6_PWM, LED7.anode
  N14: Arduino1.D7, LED8.anode
  5V: Arduino1.5V, RHT2.Vcc
  N15: LED7.cathode, R6.Pin_0
  N16: LED8.cathode, R7.Pin_0
  N17: LED9.cathode, R8.Pin_0
  N18: LED10.cathode, R9.Pin_0
