# Fritzing sketch UserBot_DCMotor (saved by Fritzing 0.9.3b)
breadboards: 1

parts:
  Arduino_w/UserBot_Shield = Arduino Uno (Rev3)
  M1 = DC Motor
  Q1 = MOSFET-NCHANNEL [package=to220v]
  P1 = Power Jack [package=power_jack_slot]

nets:
  N1: Arduino_w/UserBot_Shield.D5_PWM, Q1.G
  GND: Arduino_w/UserBot_Shield.GND, Q1.S, P1.GNDBREAK, P1.GND
  N2: M1.pin_1, P1.PWR
  N3: M1.pin_2, Q1.D
