# Fritzing sketch UserBot_1Buttons_1LM35_1LED (saved by Fritzing 0.9.3b)
breadboards: 1

parts:
  Arduino_w/UserBot_Shield = Arduino Uno (Rev3)
  S3 = Pushbutton [package="[THT]"]
  R1 = Resistor [tolerance=±5% resistance=10k package=THT]
  T1 = LM35 Temperature Sensor [package="TO92 [THT]"]
  LED1 = smd LED [color="Red (633nm)" package="0805 [SMD]"]
  R2 = Resistor [tolerance=±5% resistance=240 package=THT]

nets:
  N1: Arduino_w/UserBot_Shield.A0, S3.Pin_3, S3.Pin_4, R1.Pin_1
  N2: Arduino_w/UserBot_Shield.A1, T1.Vout
  GND: Arduino_w/UserBot_Shield.GND, R1.Pin_0, T1.GND, LED1.cathode
  N3: Arduino_w/UserBot_Shield.D3_PWM, R2.Pin_0
  N4: Arduino_w/UserBot_Shield.5V, S3.Pin_1, S3.Pin_2, T1.+Vs
  N5: LED1.anode, R2.Pin_1

// code stored in the sketch: Untitled2.ino

